// Logisim project hw4.circ as structural Verilog: 5 circuits, main circuit main
module main (
  input  Reset,
  input  [15:0] Four,
  input  [15:0] ZERO
);

  wire clk, undriven_2, WE;
  wire [1:0] M1;
  wire [2:0] ALUOp, rd, rs, rt, shamt;
  wire [3:0] Control_p1;
  wire [5:0] imm;
  wire [11:0] j;
  wire [15:0] adder_1_out, ALUResult, bit_extender_1_out, PC, RAMData, ReadData1, ReadData2, rom_1_data,
       undriven, WriteData;

  Clock clock_1 (.out(clk));
  Register #(.width(16), .trigger("falling")) u_PC (.D(adder_1_out), .Q(PC), .clk(clk), .clr(Reset));  // open: en
  Adder #(.width(16)) adder_1 (.a(Four), .b(PC), .out(adder_1_out));  // open: cin, cout
  assign bit_extender_1_out = {{10{1'b0}}, imm};  // Bit_Extender bit_extender_1
  // Control Control: pin names not known; wires that end beside it: Control_p1, M1
  Multiplexer #(.select(2), .width(16), .enable("false")) multiplexer_1 (
    .in0(ReadData2), .in1(bit_extender_1_out), .in2(ZERO), .sel(M1));  // open: in3, out
  ROM #(.addrWidth(16), .dataWidth(16)) rom_1 (.addr(PC), .data(rom_1_data));  // open: sel
  RF RF (
    .ReadReg1(rs), .ReadReg2(rt), .WriteReg(rd), .WriteData(WriteData), .RegWriteEnable(WE), .clk(clk),
    .Reset(Reset), .ReadData1(ReadData1), .ReadData2(ReadData2));
  ALU ALU (.OpType(ALUOp), .op1(ReadData1), .op2(undriven), .shamt(shamt), .OutputData(ALUResult));
  InstrDecoder InstrDecoder (
    .ROMInput(rom_1_data), .op(Control_p1), .rs(rs), .rt(rt), .rd(rd), .shamt(shamt), .j(j), .imm(imm));
  Multiplexer #(.width(16), .enable("false")) multiplexer_2 (
    .in0(ALUResult), .in1(RAMData), .out(WriteData), .sel(undriven_2));
  RAM #(.addrWidth(16), .dataWidth(16)) ram_1 (.addr(ALUResult), .data(RAMData));  // open: sel, clk, ld, clr

  // Other names for the same wires on the sheet: res = Reset
endmodule

module ALU (
  input  [2:0] OpType,
  input  [15:0] op1,
  input  [15:0] op2,
  input  [2:0] shamt,
  output [15:0] OutputData
);

  wire [3:0] bit_extender_1_out;
  wire [15:0] adder_1_out, not_1_out, shifter_1_out, shifter_2_out, subtractor_1_out, xor_1_out;

  assign bit_extender_1_out = {{1{1'b0}}, shamt};  // Bit_Extender bit_extender_1
  Adder #(.width(16)) adder_1 (.a(op1), .b(op2), .out(adder_1_out));  // open: cin, cout
  Subtractor #(.width(16)) subtractor_1 (.a(op1), .b(op2), .out(subtractor_1_out));  // open: bin, bout
  assign not_1_out = ~op1;  // NOT_Gate not_1, 16 bits wide
  assign xor_1_out = op1 ^ op2;  // XOR_Gate xor_1, 16 bits wide
  Shifter #(.width(16)) shifter_1 (.in(op1), .\dist (bit_extender_1_out), .out(shifter_1_out));
  Shifter #(.width(16), .shift("ar")) shifter_2 (.in(op1), .\dist (bit_extender_1_out), .out(shifter_2_out));
  Multiplexer #(.select(3), .width(16), .enable("false")) multiplexer_1 (
    .in0(adder_1_out), .in1(subtractor_1_out), .in2(not_1_out), .in3(xor_1_out), .in4(shifter_1_out),
    .in5(shifter_2_out), .out(OutputData), .sel(OpType));  // open: in6, in7

  // Other names for the same wires on the sheet: OT[2:0] = OpType
endmodule

module RF (
  input  [2:0] ReadReg1,
  input  [2:0] ReadReg2,
  input  [2:0] WriteReg,
  input  [15:0] WriteData,
  input  RegWriteEnable,
  input  clk,
  input  Reset,
  output [15:0] ReadData1,
  output [15:0] ReadData2
);

  wire and_1_out, and_2_out, and_3_out, and_4_out, and_5_out, and_6_out, and_7_out, and_8_out,
       decoder_1_out0, decoder_1_out1, decoder_1_out2, decoder_1_out3, decoder_1_out4, decoder_1_out5,
       decoder_1_out6, decoder_1_out7;
  wire [15:0] register_1_q, register_2_q, register_3_q, register_4_q, register_5_q, register_6_q,
       register_7_q, register_8_q;

  Decoder #(.select(3), .enable("false")) decoder_1 (
    .out0(decoder_1_out0), .out1(decoder_1_out1), .out2(decoder_1_out2), .out3(decoder_1_out3),
    .out4(decoder_1_out4), .out5(decoder_1_out5), .out6(decoder_1_out6), .out7(decoder_1_out7), .sel(WriteReg));
  and and_1 (and_1_out, decoder_1_out0, RegWriteEnable);
  and and_2 (and_2_out, decoder_1_out1, RegWriteEnable);
  and and_3 (and_3_out, decoder_1_out2, RegWriteEnable);
  and and_4 (and_4_out, decoder_1_out3, RegWriteEnable);
  and and_5 (and_5_out, decoder_1_out4, RegWriteEnable);
  and and_6 (and_6_out, decoder_1_out5, RegWriteEnable);
  and and_7 (and_7_out, decoder_1_out6, RegWriteEnable);
  and and_8 (and_8_out, decoder_1_out7, RegWriteEnable);
  Register #(.width(16), .trigger("falling")) register_1 (
    .D(WriteData), .en(and_1_out), .Q(register_1_q), .clk(clk), .clr(Reset));
  Register #(.width(16), .trigger("falling")) register_2 (
    .D(WriteData), .en(and_2_out), .Q(register_2_q), .clk(clk), .clr(Reset));
  Register #(.width(16), .trigger("falling")) register_3 (
    .D(WriteData), .en(and_3_out), .Q(register_3_q), .clk(clk), .clr(Reset));
  Register #(.width(16), .trigger("falling")) register_4 (
    .D(WriteData), .en(and_4_out), .Q(register_4_q), .clk(clk), .clr(Reset));
  Register #(.width(16), .trigger("falling")) register_5 (
    .D(WriteData), .en(and_5_out), .Q(register_5_q), .clk(clk), .clr(Reset));
  Register #(.width(16), .trigger("falling")) register_6 (
    .D(WriteData), .en(and_6_out), .Q(register_6_q), .clk(clk), .clr(Reset));
  Register #(.width(16), .trigger("falling")) register_7 (
    .D(WriteData), .en(and_7_out), .Q(register_7_q), .clk(clk), .clr(Reset));
  Register #(.width(16), .trigger("falling")) register_8 (
    .D(WriteData), .en(and_8_out), .Q(register_8_q), .clk(clk), .clr(Reset));
  // Probe on register_1_q
  // Probe on register_2_q
  // Probe on register_3_q
  // Probe on register_4_q
  // Probe on register_5_q
  // Probe on register_6_q
  // Probe on register_7_q
  // Probe on register_8_q
  Multiplexer #(.select(3), .width(16), .enable("false")) multiplexer_1 (
    .in0(register_1_q), .in1(register_2_q), .in2(register_3_q), .in3(register_4_q), .in4(register_5_q),
    .in5(register_6_q), .in6(register_7_q), .in7(register_8_q), .out(ReadData1), .sel(ReadReg1));
  Multiplexer #(.select(3), .width(16), .enable("false")) multiplexer_2 (
    .in0(register_1_q), .in1(register_2_q), .in2(register_3_q), .in3(register_4_q), .in4(register_5_q),
    .in5(register_6_q), .in6(register_7_q), .in7(register_8_q), .out(ReadData2), .sel(ReadReg2));

  // Other names for the same wires on the sheet: data[15:0] = WriteData; R1[2:0] = ReadReg1; R2[2:0] = ReadReg2;
  //   WE = RegWriteEnable
endmodule

module InstrDecoder (
  input  [15:0] ROMInput,
  output [3:0] op,
  output [2:0] rs,
  output [2:0] rt,
  output [2:0] rd,
  output [2:0] shamt,
  output [11:0] j,
  output [5:0] imm
);


  assign imm = ROMInput[5:0];
  assign j = ROMInput[11:0];
  assign op = ROMInput[15:12];
  assign rd = ROMInput[5:3];
  assign rs = ROMInput[11:9];
  assign rt = ROMInput[8:6];
  assign shamt = ROMInput[2:0];
endmodule

module Control (
  input  [3:0] op,
  input  [2:0] ALUOp,
  output M1,
  output M2
);

  wire add, addi, blt, bne, \input , j, jal, jr, lw, \not , \output , sll, sra, sub, sw, \xor ;

  and u_not (\not , ~op[3], ~op[2], ~op[1], ~op[0]);  // AND_Gate
  and u_xor (\xor , ~op[3], ~op[2], ~op[1], op[0]);  // AND_Gate
  and u_add (add, ~op[3], ~op[2], op[1], op[0]);  // AND_Gate
  and u_addi (addi, ~op[3], ~op[2], op[1], ~op[0]);  // AND_Gate
  or or_1 (M1, ~\xor , addi, ~add, ~sub, lw, sw, ~bne, ~bne);  // OR_Gate
  and u_sub (sub, ~op[3], op[2], ~op[1], ~op[0]);  // AND_Gate
  // NOR_Gate nor_1 has open pins: out=M2
  and u_sra (sra, ~op[3], op[2], ~op[1], op[0]);  // AND_Gate
  and u_lw (lw, ~op[3], op[2], op[1], op[0]);  // AND_Gate
  and u_sll (sll, ~op[3], op[2], op[1], ~op[0]);  // AND_Gate
  and u_sw (sw, op[3], ~op[2], ~op[1], ~op[0]);  // AND_Gate
  and u_j (j, op[3], ~op[2], ~op[1], op[0]);  // AND_Gate
  and u_jr (jr, op[3], ~op[2], op[1], op[0]);  // AND_Gate
  and u_jal (jal, op[3], ~op[2], op[1], ~op[0]);  // AND_Gate
  and u_bne (bne, op[3], op[2], ~op[1], ~op[0]);  // AND_Gate
  and u_blt (blt, op[3], op[2], ~op[1], op[0]);  // AND_Gate
  and u_input (\input , op[3], op[2], op[1], ~op[0]);  // AND_Gate
  and u_output (\output , op[3], op[2], op[1], op[0]);
endmodule
